// Logisim project e32.circ as structural Verilog: 8 circuits, main circuit main
module main (
);

  wire CClock, isADD, isDIV, isJMP, isMOV, isMUL, isSUB, RegAEnabled, RegBEnabled, RegCEnabled, RegDEnabled,
       RegEEnabled;
  wire [2:0] priority_encoder_1_out;
  wire [7:0] adder_2_out, divider_1_out, IncrementedPCValue, multiplexer_2_out, multiplier_1_out, PCValue,
       subtractor_1_out, ValueLoadA, ValueLoadB, ValueLoadC, ValueLoadD, ValueLoadE, ValueRegA, ValueRegB,
       ValueRegC, ValueRegD, ValueRegE;

  Clock clock_1 (.out(CClock));
  Adder adder_1 (.a(PCValue), .b(8'h1), .out(IncrementedPCValue));  // open: cin, cout
  Adder adder_2 (.a(ValueRegA), .b(8'h5), .out(adder_2_out));  // open: cin, cout
  Subtractor subtractor_1 (.a(ValueRegA), .b(8'h5), .out(subtractor_1_out));  // open: bin, bout
  Multiplier multiplier_1 (.a(ValueRegA), .b(8'h5), .out(multiplier_1_out));  // open: cin, cout
  Divider divider_1 (.a(ValueRegA), .b(8'h5), .out(divider_1_out));  // open: upper, rem
  InstructionDecoder instructiondecoder_1 (
    .Opcode(8'h5), .isMOV(isMOV), .isJMP(isJMP), .isADD(isADD), .isSUB(isSUB), .isMUL(isMUL), .isDIV(isDIV));
  RegEnabledDecoder regenableddecoder_1 (
    .isMOV(isMOV), .isADD(isADD), .isSUB(isSUB), .isMUL(isMUL), .isDIV(isDIV), .Operand1(8'h1),
    .RegAEnabled(RegAEnabled), .RegBEnabled(RegBEnabled), .RegCEnabled(RegCEnabled),
    .RegDEnabled(RegDEnabled), .RegEEnabled(RegEEnabled));
  Multiplexer #(.select(3), .width(8)) multiplexer_1 (
    .in0(8'h5), .in1(adder_2_out), .in2(subtractor_1_out), .in3(multiplier_1_out), .in4(divider_1_out),
    .out(ValueLoadA), .sel(priority_encoder_1_out));  // open: in5, in6, in7
  Priority_Encoder priority_encoder_1 (
    .in0(isMOV), .in1(isADD), .in2(isSUB), .in3(isMUL), .in4(isDIV), .out(priority_encoder_1_out));  // open: in5, in6, in7, en_in, gs, en_out
  Multiplexer #(.width(8)) multiplexer_2 (.in0(IncrementedPCValue), .in1(8'h1), .out(multiplexer_2_out), .sel(isJMP));
  Register PC (.D(multiplexer_2_out), .en(CClock), .clk(CClock), .Q(PCValue));  // open: clr
  Register RegA (.D(ValueLoadA), .en(RegAEnabled), .clk(CClock), .Q(ValueRegA));  // open: clr
  Register RegB (.D(ValueLoadB), .en(RegBEnabled), .clk(CClock), .Q(ValueRegB));  // open: clr
  Register RegC (.D(ValueLoadC), .en(RegCEnabled), .clk(CClock), .Q(ValueRegC));  // open: clr
  Register RegD (.D(ValueLoadD), .en(RegDEnabled), .clk(CClock), .Q(ValueRegD));  // open: clr
  Register RegE (.D(ValueLoadE), .en(RegEEnabled), .clk(CClock), .Q(ValueRegE));  // open: clr
  ROM #(.dataWidth(64)) rom_1 (.addr(PCValue));  // open: data

  // Notes on the sheet:
  //   contents of rom_1 (hex, n*v repeats v):
  //   1111111111111111
endmodule

module InstructionDecoder (
  input  [7:0] Opcode,
  output isMOV,
  output isJMP,
  output isADD,
  output isSUB,
  output isMUL,
  output isDIV
);

  Comparator comparator_1 (.a(Opcode), .b({8{1'b0}}), .eq(isMOV));  // open: gt, lt
  Comparator comparator_2 (.a(Opcode), .b(8'h1), .eq(isJMP));  // open: gt, lt
  Comparator comparator_3 (.a(Opcode), .b(8'h2), .eq(isADD));  // open: gt, lt
  Comparator comparator_4 (.a(Opcode), .b(8'h3), .eq(isSUB));  // open: gt, lt
  Comparator comparator_5 (.a(Opcode), .b(8'h4), .eq(isMUL));  // open: gt, lt
  Comparator comparator_6 (.a(Opcode), .b(8'h5), .eq(isDIV));  // open: gt, lt
endmodule

module MOVRegDecoder (
  input  isMOV,
  input  [7:0] Operand1,
  output isMOVA,
  output isMOVB,
  output isMOVC,
  output isMOVD,
  output isMOVE
);

  wire comparator_1_eq, comparator_2_eq, comparator_3_eq, comparator_4_eq, comparator_5_eq;

  Comparator comparator_1 (.a(Operand1), .b(8'h1), .eq(comparator_1_eq));  // open: gt, lt
  Comparator comparator_2 (.a(Operand1), .b(8'h2), .eq(comparator_2_eq));  // open: gt, lt
  Comparator comparator_3 (.a(Operand1), .b(8'h3), .eq(comparator_3_eq));  // open: gt, lt
  Comparator comparator_4 (.a(Operand1), .b(8'h4), .eq(comparator_4_eq));  // open: gt, lt
  Comparator comparator_5 (.a(Operand1), .b(8'h5), .eq(comparator_5_eq));  // open: gt, lt
  and and_1 (isMOVA, isMOV, comparator_1_eq);
  and and_2 (isMOVB, isMOV, comparator_2_eq);
  and and_3 (isMOVC, isMOV, comparator_3_eq);
  and and_4 (isMOVD, isMOV, comparator_4_eq);
  and and_5 (isMOVE, isMOV, comparator_5_eq);
endmodule

module ADDRegDecoder (
  input  isADD,
  input  [7:0] Operand1,
  output isADDA,
  output isADDB,
  output isADDC,
  output isADDD,
  output isADDE
);

  wire comparator_1_eq, comparator_2_eq, comparator_3_eq, comparator_4_eq, comparator_5_eq;

  Comparator comparator_1 (.a(Operand1), .b(8'h1), .eq(comparator_1_eq));  // open: gt, lt
  Comparator comparator_2 (.a(Operand1), .b(8'h2), .eq(comparator_2_eq));  // open: gt, lt
  Comparator comparator_3 (.a(Operand1), .b(8'h3), .eq(comparator_3_eq));  // open: gt, lt
  Comparator comparator_4 (.a(Operand1), .b(8'h4), .eq(comparator_4_eq));  // open: gt, lt
  Comparator comparator_5 (.a(Operand1), .b(8'h5), .eq(comparator_5_eq));  // open: gt, lt
  and and_1 (isADDA, isADD, comparator_1_eq);
  and and_2 (isADDB, isADD, comparator_2_eq);
  and and_3 (isADDC, isADD, comparator_3_eq);
  and and_4 (isADDD, isADD, comparator_4_eq);
  and and_5 (isADDE, isADD, comparator_5_eq);
endmodule

module RegEnabledDecoder (
  input  isMOV,
  input  isADD,
  input  isSUB,
  input  isMUL,
  input  isDIV,
  input  [7:0] Operand1,
  output RegAEnabled,
  output RegBEnabled,
  output RegCEnabled,
  output RegDEnabled,
  output RegEEnabled
);

  wire isADDA, isADDB, isADDC, isADDD, isADDE, isDIVA, isDIVB, isDIVC, isDIVD, isDIVE, isMOVA, isMOVB,
       isMOVC, isMOVD, isMOVE, isMULA, isMULB, isMULC, isMULD, isMULE, isSUBA, isSUBB, isSUBC, isSUBD,
       isSUBE, or_1_out, or_2_out, or_3_out, or_4_out, or_5_out, or_6_out, or_7_out, or_8_out, or_9_out,
       or_10_out, or_11_out, or_12_out, or_13_out, or_14_out, or_15_out;

  ADDRegDecoder addregdecoder_1 (
    .isADD(isADD), .Operand1(Operand1), .isADDA(isADDA), .isADDB(isADDB), .isADDC(isADDC), .isADDD(isADDD),
    .isADDE(isADDE));
  SUBRegDecoder subregdecoder_1 (
    .isSUB(isSUB), .Operand1(Operand1), .isSUBA(isSUBA), .isSUBB(isSUBB), .isSUBC(isSUBC), .isSUBD(isSUBD),
    .isSUBE(isSUBE));
  MOVRegDecoder movregdecoder_1 (
    .isMOV(isMOV), .Operand1(Operand1), .isMOVA(isMOVA), .isMOVB(isMOVB), .isMOVC(isMOVC), .isMOVD(isMOVD),
    .isMOVE(isMOVE));
  MULRegDecoder mulregdecoder_1 (
    .isMUL(isMUL), .Operand1(Operand1), .isMULA(isMULA), .isMULB(isMULB), .isMULC(isMULC), .isMULD(isMULD),
    .isMULE(isMULE));
  DIVRegDecoder divregdecoder_1 (
    .isDIV(isDIV), .Operand1(Operand1), .isDIVA(isDIVA), .isDIVB(isDIVB), .isDIVC(isDIVC), .isDIVD(isDIVD),
    .isDIVE(isDIVE));
  or or_1 (or_1_out, isADDA, isMOVA);
  or or_2 (or_2_out, isADDB, isMOVB);
  or or_3 (or_3_out, isADDC, isMOVC);
  or or_4 (or_4_out, isADDD, isMOVD);
  or or_5 (or_5_out, isADDE, isMOVE);
  or or_6 (or_6_out, or_1_out, isSUBA);
  or or_7 (or_7_out, or_2_out, isSUBB);
  or or_8 (or_8_out, or_3_out, isSUBC);
  or or_9 (or_9_out, or_4_out, isSUBD);
  or or_10 (or_10_out, or_5_out, isSUBE);
  or or_11 (or_11_out, or_6_out, isMULA);
  or or_12 (or_12_out, or_7_out, isMULB);
  or or_13 (or_13_out, or_8_out, isMULC);
  or or_14 (or_14_out, or_9_out, isMULD);
  or or_15 (or_15_out, or_10_out, isMULE);
  or or_16 (RegAEnabled, or_11_out, isDIVA);
  or or_17 (RegBEnabled, or_12_out, isDIVB);
  or or_18 (RegCEnabled, or_13_out, isDIVC);
  or or_19 (RegDEnabled, or_14_out, isDIVD);
  or or_20 (RegEEnabled, or_15_out, isDIVE);
endmodule

module SUBRegDecoder (
  input  isSUB,
  input  [7:0] Operand1,
  output isSUBA,
  output isSUBB,
  output isSUBC,
  output isSUBD,
  output isSUBE
);

  wire comparator_1_eq, comparator_2_eq, comparator_3_eq, comparator_4_eq, comparator_5_eq;

  Comparator comparator_1 (.a(Operand1), .b(8'h1), .eq(comparator_1_eq));  // open: gt, lt
  Comparator comparator_2 (.a(Operand1), .b(8'h2), .eq(comparator_2_eq));  // open: gt, lt
  Comparator comparator_3 (.a(Operand1), .b(8'h3), .eq(comparator_3_eq));  // open: gt, lt
  Comparator comparator_4 (.a(Operand1), .b(8'h4), .eq(comparator_4_eq));  // open: gt, lt
  Comparator comparator_5 (.a(Operand1), .b(8'h5), .eq(comparator_5_eq));  // open: gt, lt
  and and_1 (isSUBA, isSUB, comparator_1_eq);
  and and_2 (isSUBB, isSUB, comparator_2_eq);
  and and_3 (isSUBC, isSUB, comparator_3_eq);
  and and_4 (isSUBD, isSUB, comparator_4_eq);
  and and_5 (isSUBE, isSUB, comparator_5_eq);
endmodule

module MULRegDecoder (
  input  isMUL,
  input  [7:0] Operand1,
  output isMULA,
  output isMULB,
  output isMULC,
  output isMULD,
  output isMULE
);

  wire comparator_1_eq, comparator_2_eq, comparator_3_eq, comparator_4_eq, comparator_5_eq;

  Comparator comparator_1 (.a(Operand1), .b(8'h1), .eq(comparator_1_eq));  // open: gt, lt
  Comparator comparator_2 (.a(Operand1), .b(8'h2), .eq(comparator_2_eq));  // open: gt, lt
  Comparator comparator_3 (.a(Operand1), .b(8'h3), .eq(comparator_3_eq));  // open: gt, lt
  Comparator comparator_4 (.a(Operand1), .b(8'h4), .eq(comparator_4_eq));  // open: gt, lt
  Comparator comparator_5 (.a(Operand1), .b(8'h5), .eq(comparator_5_eq));  // open: gt, lt
  and and_1 (isMULA, isMUL, comparator_1_eq);
  and and_2 (isMULB, isMUL, comparator_2_eq);
  and and_3 (isMULC, isMUL, comparator_3_eq);
  and and_4 (isMULD, isMUL, comparator_4_eq);
  and and_5 (isMULE, isMUL, comparator_5_eq);
endmodule

module DIVRegDecoder (
  input  isDIV,
  input  [7:0] Operand1,
  output isDIVA,
  output isDIVB,
  output isDIVC,
  output isDIVD,
  output isDIVE
);

  wire comparator_1_eq, comparator_2_eq, comparator_3_eq, comparator_4_eq, comparator_5_eq;

  Comparator comparator_1 (.a(Operand1), .b(8'h1), .eq(comparator_1_eq));  // open: gt, lt
  Comparator comparator_2 (.a(Operand1), .b(8'h2), .eq(comparator_2_eq));  // open: gt, lt
  Comparator comparator_3 (.a(Operand1), .b(8'h3), .eq(comparator_3_eq));  // open: gt, lt
  Comparator comparator_4 (.a(Operand1), .b(8'h4), .eq(comparator_4_eq));  // open: gt, lt
  Comparator comparator_5 (.a(Operand1), .b(8'h5), .eq(comparator_5_eq));  // open: gt, lt
  and and_1 (isDIVA, isDIV, comparator_1_eq);
  and and_2 (isDIVB, isDIV, comparator_2_eq);
  and and_3 (isDIVC, isDIV, comparator_3_eq);
  and and_4 (isDIVD, isDIV, comparator_4_eq);
  and and_5 (isDIVE, isDIV, comparator_5_eq);
endmodule
